# Fritzing sketch YetAnotherWateringSystem.sketch (saved by Fritzing 0.9.4)
circuit board: 12.2698cm x 7.89578cm
perfboards: 1

parts:
  DHT1 = DHT22 Humidity and Temperature Sensor  # not connected
  Rail_12v = Basic FET N-Channel [part_number=IRL3705N package="TO220 [THT]"]  # not connected
  R1 = Resistor [tolerance=±5% resistance=10k package="1206 [SMD]"]
  Capacitive_Soil_Moisture_Sensor1 = DFRobot Capacitive Soil Moisture Sensor V1.0 [part_number=SEN0193]
  Capacitive_Soil_Moisture_Sensor2 = DFRobot Capacitive Soil Moisture Sensor V1.0 [part_number=SEN0193]
  Capacitive_Soil_Moisture_Sensor3 = DFRobot Capacitive Soil Moisture Sensor V1.0 [part_number=SEN0193]
  Capacitive_Soil_Moisture_Sensor4 = DFRobot Capacitive Soil Moisture Sensor V1.0 [part_number=SEN0193]
  U1 = Wemos Lolin D32
  Rail_3_3v = Basic FET N-Channel [part_number=IRL3705N package="TO220 [THT]"]

nets:
  N1: R1.Pin_0, U1.pin_4, Rail_3_3v.gate
  GND: R1.Pin_1, U1.pin_18, U1.pin_33, Rail_3_3v.source
  N2: Capacitive_Soil_Moisture_Sensor1.A, U1.pin_32
  VCC: Capacitive_Soil_Moisture_Sensor1.VCC, Capacitive_Soil_Moisture_Sensor3.VCC, Capacitive_Soil_Moisture_Sensor4.VCC
  GND_2: Capacitive_Soil_Moisture_Sensor1.GND, Capacitive_Soil_Moisture_Sensor2.GND, Capacitive_Soil_Moisture_Sensor3.GND, Capacitive_Soil_Moisture_Sensor4.GND, Rail_3_3v.drain
  N3: Capacitive_Soil_Moisture_Sensor2.VCC, U1.pin_0

custom parts:
  DFRobot Capacitive Soil Moisture Sensor V1.0: DFRobot Capacitive Soil Moisture Sensor V1.0 This product measures soil moisture levels by capacitive sensing, rather than resistive sensing like other types of moisture sensor. It is made of a corrosion resistant material giving it a long service life. Insert it into soil and impress your friends with the real-time soil moisture data! The product includes an on-board voltage regulator which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
  Wemos Lolin D32: Wemos Lolin D32 wifi and blue tooth board based on the ESP-32 cpu, digital I/Os 22, analog inputs 6, analog outputs 2 clock 240mhz, Flash 4Mbytes, lipo battery charger (500ma connection broken out on breadboard but not pcb), usb. The mounting holes are only set on the silkscreen, if you want actual holes in the pcb copy the hole from the pcb menu in parts over the top of the hole in the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
